# Fritzing sketch cwrm (saved by Fritzing 0.9.3b)
circuit board: 2.8cm x 2cm
breadboards: 1

parts:
  Q1 = NPN-Transistor [part_number=2N2222 package="TO92 [THT]"]
  R1 = Resistor [tolerance=±5% resistance=2.2k package=THT]
  R2 = Resistor [tolerance=±5% resistance=2.2k package=THT]
  J1 = female pin header, 3 pins [form="♀ (female)"]
  Q2 = NPN-Transistor [part_number=2N2222 package="TO92 [THT]"]
  R3 = Resistor [tolerance=±5% resistance=3.3k package=THT]
  R4 = Resistor [tolerance=±5% resistance=3.3k package=THT]
  U1 = ESP8266 WiFi Module [part_number=ESP8266]

nets:
  GND: Q1.E, J1.pin2, Q2.E, U1.GND
  N1: Q1.B, R1.Pin_1
  N2: Q1.C, J1.pin1
  N3: R1.Pin_0, R4.Pin_1, U1.GPIO_2
  N4: R2.Pin_0, R3.Pin_1, U1.GPIO_0
  N5: R2.Pin_1, Q2.B
  N6: J1.pin3, Q2.C
  3.3V: R3.Pin_0, R4.Pin_0, U1.VCC, U1.CH_PD

notes:
  f
  s
  - Shutter
  - GND
  - Focus
  github.com/willdurand/cwrm
  v1.1.0

custom parts:
  ESP8266 WiFi Module: Generic WiFi Module based on the ESP8266 with onboard PCB antenna and UART communications
